// Logisim project logisim_riscv.circ as structural Verilog: 14 circuits, main circuit main
module main (
  input  in_1
);

  wire clock_1_out, cpu_1_mwrite, mapmemmanager_1_displaywe;
  wire [3:0] button_4_out;
  wire [4:0] mapmemmanager_1_displayregn;
  wire [24:0] cpu_1_maddr;
  wire [31:0] cpu_1_mdataw, mapmemmanager_1_datar, mapmemmanager_1_displaywdata, screencontrol_1_out_6,
       screencontrol_1_out_7, screencontrol_1_out_8, screencontrol_1_out_9, screencontrol_1_out_10,
       screencontrol_1_out_11, screencontrol_1_out_12, screencontrol_1_out_13, screencontrol_1_out_14,
       screencontrol_1_out_15, screencontrol_1_out_16, screencontrol_1_out_17, screencontrol_1_out_18,
       screencontrol_1_out_19, screencontrol_1_out_20, screencontrol_1_out_21, screencontrol_1_out_22,
       screencontrol_1_out_23, screencontrol_1_out_24, screencontrol_1_out_25, screencontrol_1_out_26,
       screencontrol_1_out_27, screencontrol_1_out_28, screencontrol_1_out_29, screencontrol_1_out_30,
       screencontrol_1_out_31, screencontrol_1_out_32, screencontrol_1_out_33, screencontrol_1_out_34,
       screencontrol_1_out_35, screencontrol_1_out_36, screencontrol_1_out_37, screencontrol_1_r;

  Clock clock_1 (.out(clock_1_out));
  CPU cpu_1 (
    .Rst(in_1), .Clk(clock_1_out), .MDataR(mapmemmanager_1_datar), .MAddr(cpu_1_maddr),
    .MDataW(cpu_1_mdataw), .MWrite(cpu_1_mwrite));
  MapMemManager mapmemmanager_1 (
    .DataW(cpu_1_mdataw), .Addr(cpu_1_maddr), .ButtonsData(button_4_out),
    .DisplayWData(mapmemmanager_1_displaywdata), .DisplayRegN(mapmemmanager_1_displayregn),
    .DisplayWE(mapmemmanager_1_displaywe), .DataR(mapmemmanager_1_datar), .DisplayDataR(screencontrol_1_r),
    .MWrite(cpu_1_mwrite));
  ScreenControl screencontrol_1 (
    .Clk(clock_1_out), .Wdata(mapmemmanager_1_displaywdata), .Reset(in_1),
    .RegN(mapmemmanager_1_displayregn), .We(mapmemmanager_1_displaywe), .out_6(screencontrol_1_out_6),
    .out_14(screencontrol_1_out_14), .out_22(screencontrol_1_out_22), .out_30(screencontrol_1_out_30),
    .out_7(screencontrol_1_out_7), .out_15(screencontrol_1_out_15), .out_23(screencontrol_1_out_23),
    .out_31(screencontrol_1_out_31), .out_8(screencontrol_1_out_8), .out_16(screencontrol_1_out_16),
    .out_24(screencontrol_1_out_24), .out_32(screencontrol_1_out_32), .out_9(screencontrol_1_out_9),
    .out_17(screencontrol_1_out_17), .out_25(screencontrol_1_out_25), .out_33(screencontrol_1_out_33),
    .out_10(screencontrol_1_out_10), .out_18(screencontrol_1_out_18), .out_26(screencontrol_1_out_26),
    .out_34(screencontrol_1_out_34), .out_11(screencontrol_1_out_11), .out_19(screencontrol_1_out_19),
    .out_27(screencontrol_1_out_27), .out_35(screencontrol_1_out_35), .out_12(screencontrol_1_out_12),
    .out_20(screencontrol_1_out_20), .out_28(screencontrol_1_out_28), .out_36(screencontrol_1_out_36),
    .out_13(screencontrol_1_out_13), .out_21(screencontrol_1_out_21), .out_29(screencontrol_1_out_29),
    .out_37(screencontrol_1_out_37), .R(screencontrol_1_r));
  DotMatrix #(.inputtype("row"), .matrixcols(32), .matrixrows(32)) dotmatrix_1 (
    .row0(screencontrol_1_out_6), .row1(screencontrol_1_out_14), .row2(screencontrol_1_out_22),
    .row3(screencontrol_1_out_30), .row4(screencontrol_1_out_7), .row5(screencontrol_1_out_15),
    .row6(screencontrol_1_out_23), .row7(screencontrol_1_out_31), .row8(screencontrol_1_out_8),
    .row9(screencontrol_1_out_16), .row10(screencontrol_1_out_24), .row11(screencontrol_1_out_32),
    .row12(screencontrol_1_out_9), .row13(screencontrol_1_out_17), .row14(screencontrol_1_out_25),
    .row15(screencontrol_1_out_33), .row16(screencontrol_1_out_10), .row17(screencontrol_1_out_18),
    .row18(screencontrol_1_out_26), .row19(screencontrol_1_out_34), .row20(screencontrol_1_out_11),
    .row21(screencontrol_1_out_19), .row22(screencontrol_1_out_27), .row23(screencontrol_1_out_35),
    .row24(screencontrol_1_out_12), .row25(screencontrol_1_out_20), .row26(screencontrol_1_out_28),
    .row27(screencontrol_1_out_36), .row28(screencontrol_1_out_13), .row29(screencontrol_1_out_21),
    .row30(screencontrol_1_out_29), .row31(screencontrol_1_out_37));
  Button button_1 (.out(button_4_out[1]));
  Button button_2 (.out(button_4_out[3]));
  Button button_3 (.out(button_4_out[2]));
  Button button_4 (.out(button_4_out[0]));
endmodule

module RegFile (
  input  [4:0] An,
  input  [4:0] Bn,
  input  Clk,
  input  [31:0] Wdata,
  input  Reset,
  input  [4:0] Wn,
  input  We,
  output [31:0] A,
  output [31:0] B
);

  wire demultiplexer_1_out1, demultiplexer_1_out2, demultiplexer_1_out3, demultiplexer_1_out4,
       demultiplexer_1_out5, demultiplexer_1_out6, demultiplexer_1_out7, demultiplexer_1_out8,
       demultiplexer_1_out9, demultiplexer_1_out10, demultiplexer_1_out11, demultiplexer_1_out12,
       demultiplexer_1_out13, demultiplexer_1_out14, demultiplexer_1_out15, demultiplexer_1_out16,
       demultiplexer_1_out17, demultiplexer_1_out18, demultiplexer_1_out19, demultiplexer_1_out20,
       demultiplexer_1_out21, demultiplexer_1_out22, demultiplexer_1_out23, demultiplexer_1_out24,
       demultiplexer_1_out25, demultiplexer_1_out26, demultiplexer_1_out27, demultiplexer_1_out28,
       demultiplexer_1_out29, demultiplexer_1_out30, demultiplexer_1_out31;
  wire [31:0] x1_q, x2_q, x3_q, x4_q, x5_q, x6_q, x7_q, x8_q, x9_q, x10_q, x11_q, x12_q, x13_q, x14_q, x15_q,
       x16_q, x17_q, x18_q, x19_q, x20_q, x21_q, x22_q, x23_q, x24_q, x25_q, x26_q, x27_q, x28_q, x29_q,
       x30_q, x31_q;

  Demultiplexer #(.select(5), .disabled(0)) demultiplexer_1 (
    .out1(demultiplexer_1_out1), .out2(demultiplexer_1_out2), .out3(demultiplexer_1_out3),
    .out4(demultiplexer_1_out4), .out5(demultiplexer_1_out5), .out6(demultiplexer_1_out6),
    .out7(demultiplexer_1_out7), .out8(demultiplexer_1_out8), .out9(demultiplexer_1_out9),
    .out10(demultiplexer_1_out10), .out11(demultiplexer_1_out11), .out12(demultiplexer_1_out12),
    .out13(demultiplexer_1_out13), .out14(demultiplexer_1_out14), .out15(demultiplexer_1_out15),
    .out16(demultiplexer_1_out16), .out17(demultiplexer_1_out17), .out18(demultiplexer_1_out18),
    .out19(demultiplexer_1_out19), .out20(demultiplexer_1_out20), .out21(demultiplexer_1_out21),
    .out22(demultiplexer_1_out22), .out23(demultiplexer_1_out23), .out24(demultiplexer_1_out24),
    .out25(demultiplexer_1_out25), .out26(demultiplexer_1_out26), .out27(demultiplexer_1_out27),
    .out28(demultiplexer_1_out28), .out29(demultiplexer_1_out29), .out30(demultiplexer_1_out30),
    .out31(demultiplexer_1_out31), .in(1'b1), .sel(Wn), .en(We));  // open: out0
  Register #(.width(32)) x1 (.D(Wdata), .en(demultiplexer_1_out1), .Q(x1_q), .clk(Clk), .clr(Reset));
  Register #(.width(32)) x2 (.D(Wdata), .en(demultiplexer_1_out2), .Q(x2_q), .clk(Clk), .clr(Reset));
  Register #(.width(32)) x3 (.D(Wdata), .en(demultiplexer_1_out3), .Q(x3_q), .clk(Clk), .clr(Reset));
  Register #(.width(32)) x4 (.D(Wdata), .en(demultiplexer_1_out4), .Q(x4_q), .clk(Clk), .clr(Reset));
  Register #(.width(32)) x5 (.D(Wdata), .en(demultiplexer_1_out5), .Q(x5_q), .clk(Clk), .clr(Reset));
  Register #(.width(32)) x6 (.D(Wdata), .en(demultiplexer_1_out6), .Q(x6_q), .clk(Clk), .clr(Reset));
  Register #(.width(32)) x7 (.D(Wdata), .en(demultiplexer_1_out7), .Q(x7_q), .clk(Clk), .clr(Reset));
  Register #(.width(32)) x8 (.D(Wdata), .en(demultiplexer_1_out8), .Q(x8_q), .clk(Clk), .clr(Reset));
  Register #(.width(32)) x9 (.D(Wdata), .en(demultiplexer_1_out9), .Q(x9_q), .clk(Clk), .clr(Reset));
  Register #(.width(32)) x10 (.D(Wdata), .en(demultiplexer_1_out10), .Q(x10_q), .clk(Clk), .clr(Reset));
  Register #(.width(32)) x11 (.D(Wdata), .en(demultiplexer_1_out11), .Q(x11_q), .clk(Clk), .clr(Reset));
  Register #(.width(32)) x12 (.D(Wdata), .en(demultiplexer_1_out12), .Q(x12_q), .clk(Clk), .clr(Reset));
  Register #(.width(32)) x13 (.D(Wdata), .en(demultiplexer_1_out13), .Q(x13_q), .clk(Clk), .clr(Reset));
  Register #(.width(32)) x14 (.D(Wdata), .en(demultiplexer_1_out14), .Q(x14_q), .clk(Clk), .clr(Reset));
  Register #(.width(32)) x15 (.D(Wdata), .en(demultiplexer_1_out15), .Q(x15_q), .clk(Clk), .clr(Reset));
  Register #(.width(32)) x16 (.D(Wdata), .en(demultiplexer_1_out16), .Q(x16_q), .clk(Clk), .clr(Reset));
  Register #(.width(32)) x17 (.D(Wdata), .en(demultiplexer_1_out17), .Q(x17_q), .clk(Clk), .clr(Reset));
  Register #(.width(32)) x18 (.D(Wdata), .en(demultiplexer_1_out18), .Q(x18_q), .clk(Clk), .clr(Reset));
  Register #(.width(32)) x19 (.D(Wdata), .en(demultiplexer_1_out19), .Q(x19_q), .clk(Clk), .clr(Reset));
  Register #(.width(32)) x20 (.D(Wdata), .en(demultiplexer_1_out20), .Q(x20_q), .clk(Clk), .clr(Reset));
  Register #(.width(32)) x21 (.D(Wdata), .en(demultiplexer_1_out21), .Q(x21_q), .clk(Clk), .clr(Reset));
  Register #(.width(32)) x22 (.D(Wdata), .en(demultiplexer_1_out22), .Q(x22_q), .clk(Clk), .clr(Reset));
  Register #(.width(32)) x23 (.D(Wdata), .en(demultiplexer_1_out23), .Q(x23_q), .clk(Clk), .clr(Reset));
  Register #(.width(32)) x24 (.D(Wdata), .en(demultiplexer_1_out24), .Q(x24_q), .clk(Clk), .clr(Reset));
  Register #(.width(32)) x25 (.D(Wdata), .en(demultiplexer_1_out25), .Q(x25_q), .clk(Clk), .clr(Reset));
  Register #(.width(32)) x26 (.D(Wdata), .en(demultiplexer_1_out26), .Q(x26_q), .clk(Clk), .clr(Reset));
  Register #(.width(32)) x27 (.D(Wdata), .en(demultiplexer_1_out27), .Q(x27_q), .clk(Clk), .clr(Reset));
  Register #(.width(32)) x28 (.D(Wdata), .en(demultiplexer_1_out28), .Q(x28_q), .clk(Clk), .clr(Reset));
  Register #(.width(32)) x29 (.D(Wdata), .en(demultiplexer_1_out29), .Q(x29_q), .clk(Clk), .clr(Reset));
  Register #(.width(32)) x30 (.D(Wdata), .en(demultiplexer_1_out30), .Q(x30_q), .clk(Clk), .clr(Reset));
  Register #(.width(32)) x31 (.D(Wdata), .en(demultiplexer_1_out31), .Q(x31_q), .clk(Clk), .clr(Reset));
  Multiplexer #(.select(5), .width(32)) multiplexer_1 (
    .in0({32{1'b0}}), .in1(x1_q), .in2(x2_q), .in3(x3_q), .in4(x4_q), .in5(x5_q), .in6(x6_q), .in7(x7_q),
    .in8(x8_q), .in9(x9_q), .in10(x10_q), .in11(x11_q), .in12(x12_q), .in13(x13_q), .in14(x14_q),
    .in15(x15_q), .in16(x16_q), .in17(x17_q), .in18(x18_q), .in19(x19_q), .in20(x20_q), .in21(x21_q),
    .in22(x22_q), .in23(x23_q), .in24(x24_q), .in25(x25_q), .in26(x26_q), .in27(x27_q), .in28(x28_q),
    .in29(x29_q), .in30(x30_q), .in31(x31_q), .out(B), .sel(Bn));  // open: en
  Multiplexer #(.select(5), .width(32)) multiplexer_2 (
    .in0({32{1'b0}}), .in1(x1_q), .in2(x2_q), .in3(x3_q), .in4(x4_q), .in5(x5_q), .in6(x6_q), .in7(x7_q),
    .in8(x8_q), .in9(x9_q), .in10(x10_q), .in11(x11_q), .in12(x12_q), .in13(x13_q), .in14(x14_q),
    .in15(x15_q), .in16(x16_q), .in17(x17_q), .in18(x18_q), .in19(x19_q), .in20(x20_q), .in21(x21_q),
    .in22(x22_q), .in23(x23_q), .in24(x24_q), .in25(x25_q), .in26(x26_q), .in27(x27_q), .in28(x28_q),
    .in29(x29_q), .in30(x30_q), .in31(x31_q), .out(A), .sel(An));  // open: en

  // Notes on the sheet:
  //   Sorry, this is a bit huge
  //   I should've built incremental blocks
endmodule

module ImmGen (
  input  [31:0] Instr,
  input  [2:0] Type,
  output [31:0] out_3
);

  wire or_1_out;
  wire [31:0] bit_extender_1_out, bit_extender_2_out, bit_extender_3_out, bit_extender_4_out,
       multiplexer_1_out;

  assign bit_extender_1_out = {{20{1'b0}}, Instr[31:20]};  // Bit_Extender bit_extender_1
  assign bit_extender_2_out = {{20{Instr[31]}}, Instr[31:20]};  // Bit_Extender bit_extender_2
  or or_1 (or_1_out, ~Instr[4], ~Instr[14]);  // OR_Gate
  Multiplexer #(.width(32), .enable("false")) multiplexer_1 (
    .in0(bit_extender_1_out), .in1(bit_extender_2_out), .out(multiplexer_1_out), .sel(or_1_out));
  assign bit_extender_3_out = {{20{Instr[31]}}, {Instr[31:25], Instr[11:7]}};  // Bit_Extender bit_extender_3
  assign bit_extender_4_out = {{19{Instr[31]}}, {Instr[31], Instr[7], Instr[30:25], Instr[11:8], 1'b0}};  // Bit_Extender bit_extender_4
  Multiplexer #(.select(3), .width(32), .enable("false")) multiplexer_2 (
    .in0({32{1'b0}}), .in1({32{1'b0}}), .in2(multiplexer_1_out), .in3(bit_extender_3_out),
    .in4(bit_extender_4_out), .in5({Instr[31:12], {12{1'b0}}}),
    .in6({{11{1'b0}}, Instr[31], Instr[19:12], Instr[20], Instr[30:21], 1'b0}), .out(out_3), .sel(Type));  // open: in7

  // Notes on the sheet:
  //   U-type
  //   I type
  //   S type
  //   Same as S but reordered
  //   Same as U, but reordered
  //   (Only works with rv32, no extensions)
  //   Select if we should 0-extend or bit-extend based on the operation
  //   Select which Imm to use baesd on the decoded type
endmodule

module Decode (
  input  [31:0] Instr,
  output [6:0] Func7,
  output [2:0] Type,
  output [4:0] rs2,
  output [4:0] rs1,
  output [2:0] Func3,
  output [4:0] Rd
);

  wire and_1_out, and_2_out, and_3_out, and_4_out, and_5_out, and_6_out, and_7_out, or_1_out;

  and and_1 (and_1_out, ~Instr[6], Instr[5], Instr[4], ~Instr[3], ~Instr[2], Instr[0]);  // AND_Gate
  and and_2 (and_2_out, ~Instr[6], ~Instr[5], ~Instr[3], ~Instr[2], Instr[1], Instr[0]);  // AND_Gate
  and and_3 (and_3_out, Instr[6], Instr[5], ~Instr[4], ~Instr[3], Instr[2], Instr[1], Instr[0]);  // AND_Gate
  and and_4 (and_4_out, ~Instr[6], Instr[5], ~Instr[4], ~Instr[3], ~Instr[2], Instr[1], Instr[0]);  // AND_Gate
  and and_5 (and_5_out, Instr[6], Instr[5], ~Instr[4], ~Instr[3], ~Instr[2], Instr[1], Instr[0]);  // AND_Gate
  and and_6 (and_6_out, ~Instr[6], Instr[4], ~Instr[3], Instr[2], Instr[1], Instr[0]);  // AND_Gate
  and and_7 (and_7_out, Instr[6], Instr[5], ~Instr[4], Instr[3], Instr[2], Instr[1], Instr[0]);  // AND_Gate
  or or_1 (or_1_out, and_2_out, and_3_out);
  Priority_Encoder #(.disabled(0)) priority_encoder_1 (
    .in1(and_1_out), .in2(or_1_out), .in3(and_4_out), .in4(and_5_out), .in5(and_6_out), .in6(and_7_out),
    .out(Type));  // open: in0, in7, en_in, gs, en_out
  Pull_Resistor pull_resistor_1 (.node(Type));

  assign Func3 = Instr[14:12];
  assign Func7 = Instr[31:25];
  assign Rd = Instr[11:7];
  assign rs1 = Instr[19:15];
  assign rs2 = Instr[24:20];

  // Notes on the sheet:
  //   This has been found manually with the single instructions, does not work with extensions
  //   S
  //   SB
  //   U
  //   UJ
  //   R
  //   I
  //   Note: the type 0 is reserved for NOPs
  //   Type 7 is not used right now, any unknown type falls back to 0
endmodule

module Control (
  input  [31:0] Instr,
  input  [2:0] Type,
  input  [2:0] F3,
  input  [6:0] F7,
  output MemToReg,
  output MemRead,
  output [2:0] AluOp,
  output RegWrite,
  output MemWrite,
  output AluSrc,
  output BranchReg,
  output nLink,
  output AluNb,
  output [1:0] JumpType
);

  wire [2:0] and_5_out;

  and and_1 (MemRead, Instr[0], Instr[1], ~Instr[2], ~Instr[3], ~Instr[4], ~Instr[5], ~Instr[6]);  // AND_Gate
  and and_2 (MemWrite, Instr[0], Instr[1], ~Instr[2], ~Instr[3], ~Instr[4], Instr[5], ~Instr[6]);  // AND_Gate
  and and_3 (BranchReg, Instr[0], Instr[1], Instr[2], ~Instr[3], ~Instr[4], Instr[5], Instr[6]);  // AND_Gate
  and and_4 (nLink, Instr[0], Instr[1], Instr[2], ~Instr[4], Instr[5], Instr[6]);  // AND_Gate
  Multiplexer #(.select(3), .enable("false")) multiplexer_1 (
    .in0(1'b0), .in1(1'b1), .in2(1'b1), .in3(1'b0), .in4(1'b0), .in5(1'b1), .in6(1'b1), .in7(1'b0),
    .out(RegWrite), .sel(Type));
  Multiplexer #(.select(3), .enable("false")) multiplexer_2 (
    .in0(1'b1), .in1(1'b0), .in2(1'b1), .in3(1'b1), .in4(1'b0), .in5(1'b1), .in6(1'b1), .in7(1'b1),
    .out(AluSrc), .sel(Type));
  Multiplexer #(.select(3), .width(2), .enable("false")) multiplexer_3 (
    .in0(2'b00), .in1(2'b00), .in2({Instr[6], 1'b0}), .in3(2'b00), .in4(2'b01), .in5(2'b00), .in6(2'b01),
    .in7(2'b00), .out(JumpType), .sel(Type));
  assign and_5_out = {3{Instr[4]}} & F3;  // AND_Gate and_5, 3 bits wide
  Multiplexer #(.select(3), .width(3), .disabled(0), .enable("false")) multiplexer_4 (
    .in0(3'b110), .in1(F3), .in2(and_5_out), .in3(3'b000), .in4({2'b01, F3[1]}), .in5(3'b000), .in6(3'b000),
    .in7(3'b110), .out(AluOp), .sel(Type));
  Multiplexer #(.select(3), .disabled(0), .enable("false")) multiplexer_5 (
    .in0(1'b0), .in1(F7[5]), .in2(1'b0), .in3(1'b0), .in4(1'b1), .in5(1'b0), .in6(1'b0), .in7(1'b0),
    .out(AluNb), .sel(Type));

  assign MemToReg = MemRead;

  // Other names for the same wires on the sheet: Instr_t[6:0] = Instr[6:0]

  // Notes on the sheet:
  //   F75 is used to determine the sign (sometimes)
  //   Abs Rel None
  //   SLT with controlled signedness
  //   Every unsupported op (or any op that doesn't use the ALU) is set to Or
  //   Add Or
endmodule

module alu_8 (
  input  Sub,
  input  [2:0] Op,
  input  [7:0] B,
  input  [7:0] A,
  input  Cin,
  output [7:0] Z,
  output Zero,
  output Neg,
  output Cout,
  output Overflow
);

  wire alu_1_1_cout, alu_1_2_cout, alu_1_3_cout, alu_1_4_cout, alu_1_5_cout, alu_1_6_cout, alu_1_7_cout;

  alu_1 alu_1_1 (.A(A[0]), .B(B[0]), .Cin(Cin), .nB(Sub), .Op(Op), .Z(Z[0]), .Cout(alu_1_1_cout));  // open: OverFlow
  alu_1 alu_1_2 (
    .A(A[1]), .B(B[1]), .Cin(alu_1_1_cout), .nB(Sub), .Op(Op), .Z(Z[1]), .Cout(alu_1_2_cout));  // open: OverFlow
  alu_1 alu_1_3 (
    .A(A[2]), .B(B[2]), .Cin(alu_1_2_cout), .nB(Sub), .Op(Op), .Z(Z[2]), .Cout(alu_1_3_cout));  // open: OverFlow
  alu_1 alu_1_4 (
    .A(A[3]), .B(B[3]), .Cin(alu_1_3_cout), .nB(Sub), .Op(Op), .Z(Z[3]), .Cout(alu_1_4_cout));  // open: OverFlow
  alu_1 alu_1_5 (
    .A(A[4]), .B(B[4]), .Cin(alu_1_4_cout), .nB(Sub), .Op(Op), .Z(Z[4]), .Cout(alu_1_5_cout));  // open: OverFlow
  alu_1 alu_1_6 (
    .A(A[5]), .B(B[5]), .Cin(alu_1_5_cout), .nB(Sub), .Op(Op), .Z(Z[5]), .Cout(alu_1_6_cout));  // open: OverFlow
  alu_1 alu_1_7 (
    .A(A[6]), .B(B[6]), .Cin(alu_1_6_cout), .nB(Sub), .Op(Op), .Z(Z[6]), .Cout(alu_1_7_cout));  // open: OverFlow
  alu_1 alu_1_8 (.A(A[7]), .B(B[7]), .Cin(alu_1_7_cout), .nB(Sub), .Op(Op), .Z(Neg), .Cout(Cout), .OverFlow(Overflow));
  or or_1 (Zero, Z[0], Z[1], Z[2], Z[3], Z[4], Z[5], Z[6], Neg);

  assign Z[7] = Neg;
endmodule

module alu_32 (
  input  nB,
  input  [2:0] Op,
  input  [31:0] A,
  input  [31:0] B,
  output [31:0] Z,
  output Zero_Eq,
  output Overflow,
  output Lt
);

  wire alu_8_1_cout, alu_8_1_zero, alu_8_2_cout, alu_8_2_zero, alu_8_3_cout, alu_8_3_zero, alu_8_4_zero,
       comparator_1_eq, comparator_1_lt, comparator_2_lt, nor_1_out, SLTX;
  wire [4:0] bit_extender_1_out;
  wire [7:0] alu_8_1_z, alu_8_2_z;
  wire [31:0] bit_extender_2_out, bit_extender_3_out, multiplexer_2_out, shifter_1_out, shifter_2_out,
       shifter_3_out;
  wire [31:16] alu_8_3_z;

  Bit_Extender #(.in_width(32), .out_width(5)) bit_extender_1 (.in(B), .out(bit_extender_1_out));
  alu_8 alu_8_1 (
    .Z(alu_8_1_z), .Zero(alu_8_1_zero), .Cout(alu_8_1_cout), .Op(Op), .B(B[7:0]), .A(A[7:0]), .Cin(nB),
    .Sub(nB));  // open: Neg, Overflow
  alu_8 alu_8_2 (
    .Z(alu_8_2_z), .Zero(alu_8_2_zero), .Cout(alu_8_2_cout), .Op(Op), .B(B[15:8]), .A(A[15:8]),
    .Cin(alu_8_1_cout), .Sub(nB));  // open: Neg, Overflow
  alu_8 alu_8_3 (
    .Z(alu_8_3_z[23:16]), .Zero(alu_8_3_zero), .Cout(alu_8_3_cout), .Op(Op), .B(B[23:16]), .A(A[23:16]),
    .Cin(alu_8_2_cout), .Sub(nB));  // open: Neg, Overflow
  alu_8 alu_8_4 (
    .Z(alu_8_3_z[31:24]), .Zero(alu_8_4_zero), .Overflow(Overflow), .Op(Op), .B(B[31:24]), .A(A[31:24]),
    .Cin(alu_8_3_cout), .Sub(nB));  // open: Neg, Cout
  Comparator #(.width(32)) comparator_1 (.a(A), .b(B), .eq(comparator_1_eq), .lt(comparator_1_lt));  // open: gt
  Comparator #(.width(32), .mode("unsigned")) comparator_2 (.a(A), .b(B), .lt(comparator_2_lt));  // open: gt, eq
  Shifter #(.width(32)) shifter_1 (.in(A), .\dist (bit_extender_1_out), .out(shifter_1_out));
  Shifter #(.width(32), .shift("lr")) shifter_2 (.in(A), .\dist (bit_extender_1_out), .out(shifter_2_out));
  Shifter #(.width(32), .shift("ar")) shifter_3 (.in(A), .\dist (bit_extender_1_out), .out(shifter_3_out));
  and and_1 (SLTX, Op[1], ~Op[2]);  // AND_Gate
  assign bit_extender_2_out = {{31{1'b0}}, comparator_1_lt};  // Bit_Extender bit_extender_2
  assign bit_extender_3_out = {{31{1'b0}}, comparator_2_lt};  // Bit_Extender bit_extender_3
  Multiplexer #(.disabled(0), .enable("false")) multiplexer_1 (
    .in0(comparator_1_lt), .in1(comparator_2_lt), .out(Lt), .sel(Op[0]));
  Multiplexer #(.width(32), .disabled(0), .enable("false")) multiplexer_2 (
    .in0(shifter_2_out), .in1(shifter_3_out), .out(multiplexer_2_out), .sel(nB));
  nor nor_1 (nor_1_out, alu_8_1_zero, alu_8_2_zero, alu_8_3_zero, alu_8_4_zero);
  Multiplexer #(.disabled(0), .enable("false")) multiplexer_3 (
    .in0(nor_1_out), .in1(comparator_1_eq), .out(Zero_Eq), .sel(SLTX));
  Multiplexer #(.select(3), .width(32), .disabled(0), .enable("false")) multiplexer_4 (
    .in0({alu_8_3_z, alu_8_2_z, alu_8_1_z}), .in1(shifter_1_out), .in2(bit_extender_2_out),
    .in3(bit_extender_3_out), .in4({alu_8_3_z, alu_8_2_z, alu_8_1_z}), .in5(multiplexer_2_out),
    .in6({alu_8_3_z, alu_8_2_z, alu_8_1_z}), .in7({alu_8_3_z, alu_8_2_z, alu_8_1_z}), .out(Z), .sel(Op));

  // Other names for the same wires on the sheet: SLTU = Op[0]
endmodule

module add_1 (
  input  Cin,
  input  A,
  input  B,
  input  nB,
  output Z,
  output Cout
);

  wire and_1_out, and_2_out, xor_1_out, xor_2_out;

  xor xor_1 (xor_1_out, B, nB);
  xor xor_2 (xor_2_out, A, xor_1_out);
  and and_1 (and_1_out, A, xor_1_out);
  and and_2 (and_2_out, Cin, xor_2_out);
  xor xor_3 (Z, Cin, xor_2_out);
  or or_1 (Cout, and_2_out, and_1_out);
endmodule

module alu_1 (
  input  A,
  input  B,
  input  Cin,
  input  nB,
  input  [2:0] Op,
  output Z,
  output Cout,
  output OverFlow
);

  wire add_1_1_z, and_1_out, or_1_out, xor_1_out;

  add_1 add_1_1 (.Cin(Cin), .A(A), .B(B), .nB(nB), .Z(add_1_1_z), .Cout(Cout));
  xor xor_1 (xor_1_out, A, B);
  or or_1 (or_1_out, A, B);
  and and_1 (and_1_out, A, B);
  xor xor_2 (OverFlow, Cout, Cin);
  Multiplexer #(.select(3), .disabled(0), .enable("false")) multiplexer_1 (
    .in0(add_1_1_z), .in1(add_1_1_z), .in2(add_1_1_z), .in3(add_1_1_z), .in4(xor_1_out), .in5(or_1_out),
    .in6(or_1_out), .in7(and_1_out), .out(Z), .sel(Op));
endmodule

module Branch (
  input  [1:0] JumpType,
  input  Zero_Eq,
  input  Lt,
  input  [2:0] F3,
  input  [2:0] Type,
  output [1:0] Z
);

  wire and_1_out, multiplexer_1_out, or_1_out, xor_1_out;

  Multiplexer #(.disabled(0), .enable("false")) multiplexer_1 (
    .in0(Zero_Eq), .in1(Lt), .out(multiplexer_1_out), .sel(F3[2]));
  xor xor_1 (xor_1_out, multiplexer_1_out, F3[0]);
  or or_1 (or_1_out, xor_1_out, ~and_1_out);  // OR_Gate
  and and_1 (and_1_out, ~Type[0], ~Type[1], Type[2]);  // AND_Gate
  and and_2 (Z[0], JumpType[0], or_1_out);

  assign Z[1] = JumpType[1];

  // Notes on the sheet:
  //   Negate
  //   Branch Control Unit
  //   Skip if JAL/JALR
endmodule

module ScreenControl (
  input  Clk,
  input  Reset,
  input  [31:0] Wdata,
  input  We,
  input  [4:0] RegN,
  output [31:0] out_6,
  output [31:0] out_7,
  output [31:0] out_8,
  output [31:0] out_9,
  output [31:0] out_10,
  output [31:0] out_11,
  output [31:0] out_12,
  output [31:0] out_13,
  output [31:0] out_14,
  output [31:0] out_15,
  output [31:0] out_16,
  output [31:0] out_17,
  output [31:0] out_18,
  output [31:0] out_19,
  output [31:0] out_20,
  output [31:0] out_21,
  output [31:0] out_22,
  output [31:0] out_23,
  output [31:0] out_24,
  output [31:0] out_25,
  output [31:0] out_26,
  output [31:0] out_27,
  output [31:0] out_28,
  output [31:0] out_29,
  output [31:0] out_30,
  output [31:0] out_31,
  output [31:0] out_32,
  output [31:0] out_33,
  output [31:0] out_34,
  output [31:0] out_35,
  output [31:0] out_36,
  output [31:0] out_37,
  output [31:0] R
);

  wire demultiplexer_1_out0, demultiplexer_1_out1, demultiplexer_1_out2, demultiplexer_1_out3,
       demultiplexer_1_out4, demultiplexer_1_out5, demultiplexer_1_out6, demultiplexer_1_out7,
       demultiplexer_1_out8, demultiplexer_1_out9, demultiplexer_1_out10, demultiplexer_1_out11,
       demultiplexer_1_out12, demultiplexer_1_out13, demultiplexer_1_out14, demultiplexer_1_out15,
       demultiplexer_1_out16, demultiplexer_1_out17, demultiplexer_1_out18, demultiplexer_1_out19,
       demultiplexer_1_out20, demultiplexer_1_out21, demultiplexer_1_out22, demultiplexer_1_out23,
       demultiplexer_1_out24, demultiplexer_1_out25, demultiplexer_1_out26, demultiplexer_1_out27,
       demultiplexer_1_out28, demultiplexer_1_out29, demultiplexer_1_out30, demultiplexer_1_out31;

  Demultiplexer #(.select(5), .disabled(0)) demultiplexer_1 (
    .out0(demultiplexer_1_out0), .out1(demultiplexer_1_out1), .out2(demultiplexer_1_out2),
    .out3(demultiplexer_1_out3), .out4(demultiplexer_1_out4), .out5(demultiplexer_1_out5),
    .out6(demultiplexer_1_out6), .out7(demultiplexer_1_out7), .out8(demultiplexer_1_out8),
    .out9(demultiplexer_1_out9), .out10(demultiplexer_1_out10), .out11(demultiplexer_1_out11),
    .out12(demultiplexer_1_out12), .out13(demultiplexer_1_out13), .out14(demultiplexer_1_out14),
    .out15(demultiplexer_1_out15), .out16(demultiplexer_1_out16), .out17(demultiplexer_1_out17),
    .out18(demultiplexer_1_out18), .out19(demultiplexer_1_out19), .out20(demultiplexer_1_out20),
    .out21(demultiplexer_1_out21), .out22(demultiplexer_1_out22), .out23(demultiplexer_1_out23),
    .out24(demultiplexer_1_out24), .out25(demultiplexer_1_out25), .out26(demultiplexer_1_out26),
    .out27(demultiplexer_1_out27), .out28(demultiplexer_1_out28), .out29(demultiplexer_1_out29),
    .out30(demultiplexer_1_out30), .out31(demultiplexer_1_out31), .in(1'b1), .sel(RegN), .en(We));
  Register #(.width(32)) x0 (.D(Wdata), .en(demultiplexer_1_out0), .Q(out_6), .clk(Clk), .clr(Reset));
  Register #(.width(32)) x1 (.D(Wdata), .en(demultiplexer_1_out1), .Q(out_14), .clk(Clk), .clr(Reset));
  Register #(.width(32)) x2 (.D(Wdata), .en(demultiplexer_1_out2), .Q(out_22), .clk(Clk), .clr(Reset));
  Register #(.width(32)) x3 (.D(Wdata), .en(demultiplexer_1_out3), .Q(out_30), .clk(Clk), .clr(Reset));
  Register #(.width(32)) x4 (.D(Wdata), .en(demultiplexer_1_out4), .Q(out_7), .clk(Clk), .clr(Reset));
  Register #(.width(32)) x5 (.D(Wdata), .en(demultiplexer_1_out5), .Q(out_15), .clk(Clk), .clr(Reset));
  Register #(.width(32)) x6 (.D(Wdata), .en(demultiplexer_1_out6), .Q(out_23), .clk(Clk), .clr(Reset));
  Register #(.width(32)) x7 (.D(Wdata), .en(demultiplexer_1_out7), .Q(out_31), .clk(Clk), .clr(Reset));
  Register #(.width(32)) x8 (.D(Wdata), .en(demultiplexer_1_out8), .Q(out_8), .clk(Clk), .clr(Reset));
  Register #(.width(32)) x9 (.D(Wdata), .en(demultiplexer_1_out9), .Q(out_16), .clk(Clk), .clr(Reset));
  Register #(.width(32)) x10 (.D(Wdata), .en(demultiplexer_1_out10), .Q(out_24), .clk(Clk), .clr(Reset));
  Register #(.width(32)) x11 (.D(Wdata), .en(demultiplexer_1_out11), .Q(out_32), .clk(Clk), .clr(Reset));
  Register #(.width(32)) x12 (.D(Wdata), .en(demultiplexer_1_out12), .Q(out_9), .clk(Clk), .clr(Reset));
  Register #(.width(32)) x13 (.D(Wdata), .en(demultiplexer_1_out13), .Q(out_17), .clk(Clk), .clr(Reset));
  Register #(.width(32)) x14 (.D(Wdata), .en(demultiplexer_1_out14), .Q(out_25), .clk(Clk), .clr(Reset));
  Register #(.width(32)) x15 (.D(Wdata), .en(demultiplexer_1_out15), .Q(out_33), .clk(Clk), .clr(Reset));
  Register #(.width(32)) x16 (.D(Wdata), .en(demultiplexer_1_out16), .Q(out_10), .clk(Clk), .clr(Reset));
  Register #(.width(32)) x17 (.D(Wdata), .en(demultiplexer_1_out17), .Q(out_18), .clk(Clk), .clr(Reset));
  Register #(.width(32)) x18 (.D(Wdata), .en(demultiplexer_1_out18), .Q(out_26), .clk(Clk), .clr(Reset));
  Register #(.width(32)) x19 (.D(Wdata), .en(demultiplexer_1_out19), .Q(out_34), .clk(Clk), .clr(Reset));
  Register #(.width(32)) x20 (.D(Wdata), .en(demultiplexer_1_out20), .Q(out_11), .clk(Clk), .clr(Reset));
  Register #(.width(32)) x21 (.D(Wdata), .en(demultiplexer_1_out21), .Q(out_19), .clk(Clk), .clr(Reset));
  Register #(.width(32)) x22 (.D(Wdata), .en(demultiplexer_1_out22), .Q(out_27), .clk(Clk), .clr(Reset));
  Register #(.width(32)) x23 (.D(Wdata), .en(demultiplexer_1_out23), .Q(out_35), .clk(Clk), .clr(Reset));
  Register #(.width(32)) x24 (.D(Wdata), .en(demultiplexer_1_out24), .Q(out_12), .clk(Clk), .clr(Reset));
  Register #(.width(32)) x25 (.D(Wdata), .en(demultiplexer_1_out25), .Q(out_20), .clk(Clk), .clr(Reset));
  Register #(.width(32)) x26 (.D(Wdata), .en(demultiplexer_1_out26), .Q(out_28), .clk(Clk), .clr(Reset));
  Register #(.width(32)) x27 (.D(Wdata), .en(demultiplexer_1_out27), .Q(out_36), .clk(Clk), .clr(Reset));
  Register #(.width(32)) x28 (.D(Wdata), .en(demultiplexer_1_out28), .Q(out_13), .clk(Clk), .clr(Reset));
  Register #(.width(32)) x29 (.D(Wdata), .en(demultiplexer_1_out29), .Q(out_21), .clk(Clk), .clr(Reset));
  Register #(.width(32)) x30 (.D(Wdata), .en(demultiplexer_1_out30), .Q(out_29), .clk(Clk), .clr(Reset));
  Register #(.width(32)) x31 (.D(Wdata), .en(demultiplexer_1_out31), .Q(out_37), .clk(Clk), .clr(Reset));
  Multiplexer #(.select(5), .width(32), .disabled(0), .enable("false")) multiplexer_1 (
    .in0(out_6), .in1(out_14), .in2(out_22), .in3(out_30), .in4(out_7), .in5(out_15), .in6(out_23),
    .in7(out_31), .in8(out_8), .in9(out_16), .in10(out_24), .in11(out_32), .in12(out_9), .in13(out_17),
    .in14(out_25), .in15(out_33), .in16(out_10), .in17(out_18), .in18(out_26), .in19(out_34), .in20(out_11),
    .in21(out_19), .in22(out_27), .in23(out_35), .in24(out_12), .in25(out_20), .in26(out_28), .in27(out_36),
    .in28(out_13), .in29(out_21), .in30(out_29), .in31(out_37), .out(R), .sel(RegN));
endmodule

module Memory (
  input  [26:0] Addr,
  input  [31:0] DataIn,
  input  [2:0] Width,
  input  Enable,
  input  Read,
  input  Write,
  input  Clk,
  input  Rst,
  input  [31:0] MDataR,
  output [31:0] DataOut,
  output Hold,
  output [31:0] MDataW,
  output MWrite,
  output [24:0] MAddr
);

  wire and_2_out, d_ff_1_q, decoder_1_out0, decoder_1_out1, decoder_1_out2, decoder_1_out3, not_1_out,
       not_2_out, or_1_out, or_2_out, or_3_out, or_4_out, RamRead;
  wire [7:0] multiplexer_1_out, multiplexer_2_out, multiplexer_3_out, multiplexer_4_out, multiplexer_12_out,
       register_1_q_3, register_1_q_4;
  wire [15:0] multiplexer_13_out;
  wire [23:0] adder_1_out;
  wire [31:0] bit_extender_1_out, bit_extender_2_out, bit_extender_3_out, bit_extender_4_out,
       multiplexer_5_out, multiplexer_6_out, multiplexer_7_out, multiplexer_9_out, multiplexer_10_out,
       multiplexer_14_out, multiplexer_15_out, multiplexer_16_out, ram_1_data, RawOut;
  wire [31:24] register_1_q, register_1_q_2;

  // Probe on Addr
  or or_1 (or_1_out, Read, Write);
  and and_1 (RamRead, or_1_out, ~Addr[26]);  // AND_Gate
  Decoder #(.select(2), .disabled(0), .enable("false")) decoder_1 (
    .out0(decoder_1_out0), .out1(decoder_1_out1), .out2(decoder_1_out2), .out3(decoder_1_out3),
    .sel(Addr[1:0]));
  Multiplexer #(.width(8), .disabled(0), .enable("false")) multiplexer_1 (
    .in0(RawOut[7:0]), .in1(DataIn[7:0]), .out(multiplexer_1_out), .sel(decoder_1_out3));
  Multiplexer #(.width(8), .disabled(0), .enable("false")) multiplexer_2 (
    .in0(RawOut[15:8]), .in1(DataIn[7:0]), .out(multiplexer_2_out), .sel(decoder_1_out2));
  Multiplexer #(.width(8), .disabled(0), .enable("false")) multiplexer_3 (
    .in0(RawOut[23:16]), .in1(DataIn[7:0]), .out(multiplexer_3_out), .sel(decoder_1_out1));
  Multiplexer #(.width(8), .disabled(0), .enable("false")) multiplexer_4 (
    .in0(RawOut[31:24]), .in1(DataIn[7:0]), .out(multiplexer_4_out), .sel(decoder_1_out0));
  or or_2 (or_2_out, ~Width[1], ~Addr[1]);  // OR_Gate
  or or_3 (or_3_out, ~Width[1], ~Addr[0]);  // OR_Gate
  or or_4 (or_4_out, ~Width[0], ~Addr[1], ~Addr[0]);  // OR_Gate
  Multiplexer #(.select(2), .width(32), .disabled(0), .enable("false")) multiplexer_5 (
    .in0({DataIn[15:0], RawOut[15:0]}), .in1({RawOut[31:24], DataIn[15:0], RawOut[7:0]}),
    .in2({RawOut[31:16], DataIn[15:0]}), .in3({RawOut[31:8], DataIn[15:8]}), .out(multiplexer_5_out),
    .sel(Addr[1:0]));
  Multiplexer #(.select(2), .width(32), .disabled(0), .enable("false")) multiplexer_6 (
    .in0(DataIn), .in1({RawOut[31:24], DataIn[31:8]}), .in2({RawOut[31:16], DataIn[31:16]}),
    .in3({RawOut[31:8], DataIn[31:24]}), .out(multiplexer_6_out), .sel(Addr[1:0]));
  Multiplexer #(.select(2), .width(32), .disabled(0), .enable("false")) multiplexer_7 (
    .in0({DataIn[7:0], RawOut[23:0]}), .in1({DataIn[7:0], RawOut[23:0]}), .in2({DataIn[15:0], RawOut[15:0]}),
    .in3({DataIn[23:0], RawOut[7:0]}), .out(multiplexer_7_out), .sel(Addr[1:0]));
  Multiplexer #(.width(24), .disabled(0), .enable("false")) multiplexer_8 (
    .in0(Addr[25:2]), .in1(adder_1_out), .out(MAddr[23:0]), .sel(d_ff_1_q));
  Adder #(.width(24)) adder_1 (.a(Addr[25:2]), .b(24'h1), .out(adder_1_out));  // open: cin, cout
  and and_2 (and_2_out, or_2_out, or_3_out, or_4_out);
  Multiplexer #(.select(2), .width(32), .disabled(0), .enable("false")) multiplexer_9 (
    .in0({multiplexer_4_out, multiplexer_3_out, multiplexer_2_out, multiplexer_1_out}),
    .in1(multiplexer_5_out), .in2(multiplexer_6_out), .in3(multiplexer_6_out), .out(multiplexer_9_out),
    .sel(Width[1:0]));
  Multiplexer #(.select(2), .width(32), .disabled(0), .enable("false")) multiplexer_10 (
    .in0({DataIn[7:0], RawOut[23:0]}), .in1({DataIn[7:0], RawOut[23:0]}), .in2(multiplexer_7_out),
    .in3(multiplexer_7_out), .out(multiplexer_10_out), .sel(Width[1:0]));
  and and_3 (Hold, ~d_ff_1_q, ~and_2_out, Enable);  // AND_Gate
  Multiplexer #(.width(32), .disabled(0), .enable("false")) multiplexer_11 (
    .in0(multiplexer_9_out), .in1(multiplexer_10_out), .out(MDataW), .sel(d_ff_1_q));
  D_Flip_Flop d_ff_1 (.clk(Clk), .D(Hold), .Q(d_ff_1_q), .reset(Rst));  // open: Qn, preset, en
  not not_1 (not_1_out, d_ff_1_q);
  Register #(.width(32)) register_1 (
    .D(RawOut), .en(not_1_out), .Q({register_1_q, register_1_q_2, register_1_q_3, register_1_q_4}),
    .clk(Clk), .clr(Rst));
  and and_4 (MAddr[24], Enable, Addr[26]);
  Multiplexer #(.select(2), .width(8), .disabled(0), .enable("false")) multiplexer_12 (
    .in0(RawOut[31:24]), .in1(RawOut[23:16]), .in2(RawOut[15:8]), .in3(RawOut[7:0]),
    .out(multiplexer_12_out), .sel(Addr[1:0]));
  Multiplexer #(.select(2), .width(16), .disabled(0), .enable("false")) multiplexer_13 (
    .in0(RawOut[31:16]), .in1(RawOut[23:8]), .in2(RawOut[15:0]), .in3({register_1_q_4, RawOut[31:24]}),
    .out(multiplexer_13_out), .sel(Addr[1:0]));
  Multiplexer #(.select(2), .width(32), .disabled(0), .enable("false")) multiplexer_14 (
    .in0(RawOut), .in1({register_1_q_2, register_1_q_3, register_1_q_4, RawOut[31:24]}),
    .in2({register_1_q_3, register_1_q_4, RawOut[31:16]}), .in3({register_1_q_4, RawOut[31:8]}),
    .out(multiplexer_14_out), .sel(Addr[1:0]));
  not not_2 (not_2_out, Addr[26]);
  assign bit_extender_1_out = {{24{1'b0}}, multiplexer_12_out};  // Bit_Extender bit_extender_1
  assign bit_extender_2_out = {{24{multiplexer_12_out[7]}}, multiplexer_12_out};  // Bit_Extender bit_extender_2
  assign bit_extender_3_out = {{16{1'b0}}, multiplexer_13_out};  // Bit_Extender bit_extender_3
  assign bit_extender_4_out = {{16{multiplexer_13_out[15]}}, multiplexer_13_out};  // Bit_Extender bit_extender_4
  Multiplexer #(.width(32), .disabled(0), .enable("false")) multiplexer_15 (
    .in0(bit_extender_1_out), .in1(bit_extender_2_out), .out(multiplexer_15_out), .sel(Width[2]));
  Multiplexer #(.width(32), .disabled(0), .enable("false")) multiplexer_16 (
    .in0(bit_extender_3_out), .in1(bit_extender_4_out), .out(multiplexer_16_out), .sel(Width[2]));
  RAM #(.addrWidth(24), .dataWidth(32), .bus("separate")) ram_1 (
    .addr(MAddr[23:0]), .din(MDataW), .data(ram_1_data), .str(Write), .sel(not_2_out), .clk(Clk),
    .ld(RamRead), .clr(Rst));
  Multiplexer #(.select(2), .width(32), .disabled(0), .enable("false")) multiplexer_17 (
    .in0(multiplexer_15_out), .in1(multiplexer_16_out), .in2(multiplexer_14_out), .in3(multiplexer_14_out),
    .out(DataOut), .sel(Width[1:0]));
  Multiplexer #(.width(32), .disabled(0), .enable("false")) multiplexer_18 (
    .in0(ram_1_data), .in1(MDataR), .out(RawOut), .sel(Addr[26]));

  assign MWrite = Write;

  // Other names for the same wires on the sheet: Offset[1:0] = Addr[1:0]; RamnMap = Addr[26];
  //   RawAddr[23:0] = MAddr[23:0]; RawWrite[31:0] = MDataW; Width_t[1:0] = Width[1:0]; Unsigned = Width[2]

  // Notes on the sheet:
  //   Needs next word?
  //   Write Value generation
  //   Raw Memory
  //   Accounts for offset (first half) and splitting (second half)
  //   It's a bit complex but it's all just wires and mutexes
  //   The base idea is simple, take the value from RAM and
  //   Replace the written part with some of the input value
  //   RAM Data
  //   Mapped Data
  //   Out Value Generation
  //   Accounts for offset and splitting
  //   For the splitting it stores the first value in a register
  //   This means that any read/write can be double cycle
  //   If the data it's writing spans two different RAM lcoations
endmodule

// MDataR
module CPU (
  input  Clk,
  input  Rst,
  input  [31:0] MDataR,
  output [24:0] MAddr,
  output [31:0] MDataW,
  output MWrite
);

  wire alu_32_1_lt, alu_32_1_zero_eq, AluInv, AluSrc, BranchReg, Clk_t, ClkHold, MemRead, MemToReg, MemWrite,
       nlink, not_1_out, or_1_out, RegWrite;
  wire [1:0] Branch, branch_1_z, multiplexer_2_out, multiplexer_2_out_3, multiplexer_2_out_4,
       multiplexer_2_out_5, multiplexer_2_out_6, multiplexer_2_out_7, multiplexer_2_out_8,
       multiplexer_2_out_9;
  wire [2:0] AluOp, decode_1_func3, decode_1_type;
  wire [4:0] decode_1_rd, decode_1_rs1, decode_1_rs2;
  wire [6:0] decode_1_func7;
  wire [15:0] adder_2_out, multiplexer_1_out, multiplexer_2_out_2, PC_q;
  wire [17:2] NextInstr;
  wire [26:0] bit_extender_1_out;
  wire [31:0] alu_32_1_z, immgen_1_out_3, memory_1_dataout, multiplexer_3_out, multiplexer_4_out,
       multiplexer_5_out, regfile_1_a, regfile_1_b, rom_1_data;

  Multiplexer #(.select(2), .width(16), .disabled(0), .enable("false")) multiplexer_1 (
    .in0(NextInstr), .in1(adder_2_out), .in2(multiplexer_2_out_2), .in3(multiplexer_2_out_2),
    .out(multiplexer_1_out), .sel(branch_1_z));
  Clock clock_1 (.out(Clk_t));
  not not_1 (not_1_out, ClkHold);
  Register #(.width(16), .trigger("falling")) PC (
    .D(multiplexer_1_out), .en(not_1_out), .Q(PC_q), .clk(Clk_t), .clr(Rst));
  Adder #(.width(16)) adder_1 (.a(16'h1), .b(PC_q), .out(NextInstr), .cin(1'b0));  // open: cout
  Adder #(.width(16)) adder_2 (.a(multiplexer_2_out_2), .b(PC_q), .out(adder_2_out), .cin(1'b0));  // open: cout
  ROM #(.addrWidth(16), .dataWidth(32)) rom_1 (.addr(PC_q), .data(rom_1_data), .sel(1'b1));
  Decode decode_1 (
    .Instr(rom_1_data), .Type(decode_1_type), .Rd(decode_1_rd), .Func7(decode_1_func7), .rs2(decode_1_rs2),
    .rs1(decode_1_rs1), .Func3(decode_1_func3));
  RegFile regfile_1 (
    .Bn(decode_1_rs2), .Clk(Clk_t), .Wdata(multiplexer_4_out), .Wn(decode_1_rd), .We(RegWrite),
    .A(regfile_1_a), .B(regfile_1_b), .An(decode_1_rs1), .Reset(Rst));
  ImmGen immgen_1 (.out_3(immgen_1_out_3), .Instr(rom_1_data), .Type(decode_1_type));
  Control control_1 (
    .Instr(rom_1_data), .Type(decode_1_type), .F3(decode_1_func3), .F7(decode_1_func7), .MemToReg(MemToReg),
    .MemRead(MemRead), .RegWrite(RegWrite), .MemWrite(MemWrite), .AluSrc(AluSrc), .AluOp(AluOp),
    .BranchReg(BranchReg), .nLink(nlink), .JumpType(Branch), .AluNb(AluInv));
  Multiplexer #(.width(32), .disabled(0), .enable("false")) multiplexer_2 (
    .in0(immgen_1_out_3), .in1(regfile_1_a),
    .out({multiplexer_2_out_9, multiplexer_2_out_8, multiplexer_2_out_7, multiplexer_2_out_6, multiplexer_2_out_5, multiplexer_2_out_4, multiplexer_2_out_3, multiplexer_2_out_2, multiplexer_2_out}),
    .sel(BranchReg));
  Multiplexer #(.width(32), .disabled(0), .enable("false")) multiplexer_3 (
    .in0(regfile_1_b), .in1(immgen_1_out_3), .out(multiplexer_3_out), .sel(AluSrc));
  alu_32 alu_32_1 (
    .Zero_Eq(alu_32_1_zero_eq), .Op(AluOp), .A(regfile_1_a), .B(multiplexer_3_out), .Z(alu_32_1_z),
    .Lt(alu_32_1_lt), .nB(AluInv));  // open: Overflow
  Branch branch_1 (
    .Zero_Eq(alu_32_1_zero_eq), .Lt(alu_32_1_lt), .JumpType(Branch), .F3(decode_1_func3),
    .Type(decode_1_type), .Z(branch_1_z));
  Bit_Extender #(.in_width(32), .out_width(27)) bit_extender_1 (.in(alu_32_1_z), .out(bit_extender_1_out));
  Multiplexer #(.width(32), .disabled(0), .enable("false")) multiplexer_4 (
    .in0(multiplexer_5_out), .in1({{14{1'b0}}, NextInstr, 2'b00}), .out(multiplexer_4_out), .sel(nlink));
  Memory memory_1 (
    .Addr(bit_extender_1_out), .DataIn(regfile_1_b), .Width(decode_1_func3), .Enable(or_1_out),
    .Read(MemRead), .Write(MemWrite), .Clk(Clk_t), .Rst(Rst), .MDataR(MDataR), .DataOut(memory_1_dataout),
    .Hold(ClkHold), .MDataW(MDataW), .MAddr(MAddr), .MWrite(MWrite));
  or or_1 (or_1_out, MemRead, MemWrite);
  Multiplexer #(.width(32), .enable("false")) multiplexer_5 (
    .in0(alu_32_1_z), .in1(memory_1_dataout), .out(multiplexer_5_out), .sel(MemToReg));

  // Notes on the sheet:
  //   Rst: pull=down
  //   I don't support interupts
  //   This has been coded so that every 0-instruction is a NOP
  //   contents of rom_1 (hex, n*v repeats v):
  //   40001b7 228000ef f00413 f00493 b00913 b00993 100a13 100a93 20000ef 68000ef ffdff06f 6f 50663
  //   fff50513 ff9ff06f 8067 2000293 fff28293 313 929663 800003b7 83d333 300393 41228e33 7e7663 40000e37
  //   1c30333 41328e33 7e7463 230313 229393 3383b3 63a023 fc0290e3 8067 1001c283 32f313 6030263 ffe30313
  //   2034863 4098c63 fff98993 299313 330333 32383 238393 732023 c32e03 ffee0e13 1c32623 300006f fe398313
  //   2030463 198993 299313 330333 ffc32383 ffe38393 fe732e23 832e03 2e0e13 1c32423 22d313 6030663
  //   ffe30313 2034a63 6090063 fff90913 291313 330333 32383 400002b7 5383b3 732023 c32e03 405e0e33 1c32623
  //   340006f fe390313 2030663 190913 291313 330333 ffc32383 400002b7 405383b3 fe732e23 832e03 5e0e33
  //   1c32423 14402b3 1548333 2000393 35863 313 100a93 100006f 734663 1f00313 fff00a93 2d863 293 100a13
  //   500006f 72c863 1f00293 fff00a13 400006f 100393 729e63 412303b3 300e13 3c3f663 128293 100a13 200006f
  //   1e00393 729c63 413303b3 300e13 1c3f663 fff28293 fff00a13 249e13 3e0e33 e2e83 80000f37 8f5fb3 1feceb3
  //   1de2023 231e13 3e0e33 e2e83 5f5fb3 1feceb3 1de2023 28413 30493 8067 1a023 576742b7 a8028293 51a223
  //   755432b7 a8028293 51a423 575632b7 38028293 51a623 555432b7 90028293 51a823 556742b7 b0028293 51aa23
  //   1ac23 1ae23 777772b7 28293 251a023 554422b7 28293 251a223 657722b7 28293 251a423 551122b7 28293
  //   251a623 577772b7 28293 251a823 201aa23 477752b7 bb828293 251ac23 455472b7 8a828293 251ae23 457672b7
  //   92828293 451a023 456462b7 a2828293 451a223 775752b7 bb828293 451a423 401a623 54b802b7 1f028293
  //   451a823 569002b7 2e828293 451aa23 569002b7 5f428293 451ac23 559012b7 f1e28293 451ae23 74b812b7
  //   a0a28293 651a023 12b7 a0a28293 651a223 577712b7 ffe28293 651a423 755402b7 6ac28293 651a623 556602b7
  //   4a428293 651a823 555402b7 20828293 651aa23 575702b7 1f028293 651ac23 601ae23 8067
  //   Instruction Decode
  //   Control Unit
  //   Logisim does not support 32 bits of address
  //   Remove the first 2 bits, we don't support compressed operations
  //   Mapped Memroy pins
  //   Made by: Rossi Lorenzo (Unimore)
endmodule

// WData
module MapMemManager (
  input  [31:0] DataW,
  input  MWrite,
  input  [24:0] Addr,
  input  [31:0] DisplayDataR,
  input  [3:0] ButtonsData,
  output [31:0] DisplayWData,
  output [4:0] DisplayRegN,
  output DisplayWE,
  output [31:0] DataR
);

  wire [7:0] bit_extender_1_out;

  assign bit_extender_1_out = {{4{1'b0}}, ButtonsData};  // Bit_Extender bit_extender_1
  and and_1 (DisplayWE, Addr[24], MWrite, ~Addr[6]);  // AND_Gate
  Multiplexer #(.width(32), .disabled(0), .enable("false")) multiplexer_1 (
    .in0(DisplayDataR), .in1({bit_extender_1_out, {24{1'b0}}}), .out(DataR), .sel(Addr[6]));

  assign DisplayRegN = Addr[4:0];
  assign DisplayWData = DataW;

  // Other names for the same wires on the sheet: En = Addr[24]
endmodule
